# Fritzing sketch aquarium (saved by Fritzing 0.9.0b)
circuit board: 10cm x 6.5cm
breadboards: 1

parts:
  S5 = Pushbutton [package="[THT]"]
  S4 = Pushbutton [package="[THT]"]
  S3 = Pushbutton [package="[THT]"]
  S2 = Pushbutton [package="[THT]"]
  S1 = Pushbutton [package="[THT]"]
  R7 = Resistor [tolerance=±5% resistance=2.2k package=THT]
  R6 = Resistor [tolerance=±5% resistance=1k package=THT]
  R5 = Resistor [tolerance=±5% resistance=680 package=THT]
  R4 = Resistor [tolerance=±5% resistance=330 package=THT]
  R3 = Resistor [tolerance=±5% resistance=2k package=THT]
  R11 = Resistor [tolerance=±5% resistance=1k package=THT]
  R12 = Resistor [tolerance=±5% resistance=1k package=THT]
  DHT1 = DHT11 Humitidy and Temperature Sensor
  RTC1 = DS1307 RTC Breakout  # not connected
  LED1 = LED - 5mm [color="Green (555nm)" package="5 mm [THT]"]
  LED2 = LED - 5mm [color="Red (633nm)" package="5 mm [THT]"]
  LED3 = LED - 5mm [color="Yellow (595nm)" package="5 mm [THT]"]
  LED4 = LED - 5mm [color="Yellow (592nm)" package="5 mm [THT]"]
  R14 = Resistor [tolerance=±5% resistance=1k package=THT]
  J1 = Piezo Speaker
  R13 = Resistor [tolerance=±5% resistance=1k package=THT]
  LCD1 = LCD screen
  R15 = Resistor [tolerance=±5% resistance=220 package=THT]
  R16 = Trimmer Potentiometer [maximum_resistance=10kΩ package=THT]
  Componente1 = Arduino Uno (Rev3)

nets:
  N1: S5.Pin_1, S5.Pin_2
  N2: S5.Pin_3, S5.Pin_4, R7.Pin_1
  N3: S4.Pin_1, S4.Pin_2, S3.Pin_1, S3.Pin_2, S2.Pin_1, S2.Pin_2, S1.Pin_1, S1.Pin_2, Componente1.A1
  N4: S4.Pin_3, S4.Pin_4, R7.Pin_0, R6.Pin_1
  N5: S3.Pin_3, S3.Pin_4, R6.Pin_0, R5.Pin_1
  N6: S2.Pin_3, S2.Pin_4, R5.Pin_0, R4.Pin_1
  N7: S1.Pin_3, S1.Pin_4, R4.Pin_0, R3.Pin_1
  N8: R3.Pin_0, LCD1.VDD, R16.leg2
  N9: R11.Pin_0, R12.Pin_0
  N10: R11.Pin_1, LED1.anode
  N11: R12.Pin_1, LED2.anode
  VDD: DHT1.VDD, R15.Pin_0, Componente1.5V
  N12: DHT1.DATA, Componente1.A0
  GND: DHT1.GND, J1.pin2, LCD1.R/W, LCD1.LED-, R16.leg1, Componente1.GND
  N13: LED3.anode, R13.Pin_1
  N14: LED4.anode, R14.Pin_1
  N15: J1.pin1, Componente1.D7
  N16: LCD1.V0, R16.wiper
  N17: LCD1.RS, Componente1.D13/SCK
  N18: LCD1.E, Componente1.D12/MISO
  N19: LCD1.DB4, Componente1.D5_PWM
  N20: LCD1.DB5, Componente1.D4
  N21: LCD1.DB6, Componente1.D3_PWM
  N22: LCD1.DB7, Componente1.D2
  N23: LCD1.LED+, R15.Pin_1

custom parts:
  DHT11 Humitidy and Temperature Sensor: DHT11 Humidity and Temperature Sensor
  DS1307 RTC Breakout: DS1307 Real-time Clock Breakout Board with Battery
